# Fritzing sketch arduipager (saved by Fritzing 0.9.3b)
breadboards: 1

parts:
  LCD1 = LCD screen
  Part1 = Arduino Uno (Rev3) - ICSP
  U1 = 74HC595 [package="DIP16 [THT]"]
  R1 = Trimmer Potentiometer [maximum_resistance=10kΩ package=THT]
  GSM_SIM_GPSR_SMS_SIM900_SIM1 = SIM800L [package=THT]
  R3 = Resistor [tolerance=±5% resistance=220 package="1206 [SMD]"]
  Matrix_keypad1 = KEYPAD 4x4
  VCC1 = 4 x AAA Battery Mount

nets:
  GND: LCD1.VSS, LCD1.R/W, LCD1.LED-, Part1.GND, U1.GND, U1.OE, R1.leg1, GSM_SIM_GPSR_SMS_SIM900_SIM1.GND, VCC1.-
  VDD: LCD1.VDD, Part1.VIN, U1.MR, U1.VCC, R1.leg2, GSM_SIM_GPSR_SMS_SIM900_SIM1.VDD, R3.Pin_0, VCC1.+
  N1: LCD1.V0, R1.wiper
  N2: LCD1.RS, Part1.D8
  N3: LCD1.E, Part1.D9_PWM
  N4: LCD1.DB0, U1.Q0
  N5: LCD1.DB1, U1.Q1
  N6: LCD1.DB2, U1.Q2
  N7: LCD1.DB3, U1.Q3
  N8: LCD1.DB4, U1.Q4
  N9: LCD1.DB5, U1.Q5
  N10: LCD1.DB6, U1.Q6
  N11: LCD1.DB7, U1.Q7
  N12: LCD1.LED+, R3.Pin_1
  N13: Part1.A0, Matrix_keypad1.row1
  N14: Part1.A1, Matrix_keypad1.row2
  N15: Part1.A2, Matrix_keypad1.row3
  N16: Part1.A3, Matrix_keypad1.row4
  N17: Part1.D10_PWM/SS, Matrix_keypad1.col1
  N18: Part1.D11_PWM/MOSI, Matrix_keypad1.col2
  N19: Part1.D12/MISO, Matrix_keypad1.col3
  N20: Part1.D13/SCK, Matrix_keypad1.col4
  N21: Part1.D2, GSM_SIM_GPSR_SMS_SIM900_SIM1.SIM_TXD
  N22: Part1.D3_PWM, GSM_SIM_GPSR_SMS_SIM900_SIM1.SIM_RXD
  N23: Part1.D4, U1.DS
  N24: Part1.D5_PWM, U1.ST_CP
  N25: Part1.D6_PWM, U1.SH_CP
  N26: Part1.D7, GSM_SIM_GPSR_SMS_SIM900_SIM1.RST

custom parts:
  KEYPAD 4x4: Matrix keypad 16 buttons, 4 rows x 4 columns
